# Fritzing sketch Encendido de leds (saved by Fritzing 0.9.3b)
breadboards: 1

parts:
  R1 = Resistor [tolerance=±5% resistance=220 package=THT]
  R2 = Resistor [tolerance=±5% resistance=220 package=THT]
  R3 = Resistor [tolerance=±5% resistance=220 package=THT]
  S1 = Pushbutton [package="[THT]"]
  S2 = Pushbutton [package="[THT]"]
  S3 = Pushbutton [package="[THT]"]
  LED1 = LED - 5mm [color="Red (633nm)" package="5 mm [THT]"]
  VCC1 = Battery
  LED2 = LED - 5mm [color="Red (633nm)" package="5 mm [THT]"]
  LED3 = LED - 5mm [color="Red (633nm)" package="5 mm [THT]"]

nets:
  N1: R1.Pin_0, S1.Pin_1, S1.Pin_2
  N2: R1.Pin_1, R2.Pin_1, R3.Pin_1, VCC1.+
  N3: R2.Pin_0, S2.Pin_1, S2.Pin_2
  N4: R3.Pin_0, S3.Pin_1, S3.Pin_2
  N5: S1.Pin_3, S1.Pin_4, LED1.anode
  N6: S2.Pin_3, S2.Pin_4, LED2.anode
  N7: S3.Pin_3, S3.Pin_4, LED3.anode
  N8: LED1.cathode, VCC1.-, LED2.cathode, LED3.cathode
